# Fritzing sketch UltraSonic (saved by Fritzing 0.9.2b)
circuit board: 8.46667cm x 5.64444cm
breadboards: 1

parts:
  Bean = LightBlue Bean
  V1 = DC Power [voltage=5]
  V2 = DC Power [voltage=3.3V]
  Ultrasonic_Sensor = SRF05 Ultrasonic Rangefinder
  R1 = Resistor [tolerance=±5% resistance=1k package="2010 [SMD]"]
  Q1 = NPN-Transistor [package="TO92 [THT]"]
  LED1 = smd LED [color="Yellow (592nm)" package="0805 [SMD]"]
  LED2 = smd LED [color="Blue (505nm)" package="0805 [SMD]"]
  R3 = Resistor [tolerance=±5% resistance=1k package="2010 [SMD]"]
  R4 = Resistor [tolerance=±5% resistance=1k package="2010 [SMD]"]
  R5 = Resistor [tolerance=±5% resistance=1k package="2010 [SMD]"]
  R7 = Resistor [tolerance=±5% resistance=1.5k package="2010 [SMD]"]

nets:
  N1: Bean.D2, R4.Pin_1
  N2: Bean.D0, R1.Pin_0, LED2.anode, R7.Pin_1
  N3: Bean.BAT, V2.V+
  N4: Bean.GND, V2.V-
  N5: V1.V+, Ultrasonic_Sensor.VCC, R3.Pin_0
  N6: V1.V-, Ultrasonic_Sensor.GND, R1.Pin_1, Q1.C, R5.Pin_1
  N7: Ultrasonic_Sensor.Echo, R7.Pin_0
  N8: Q1.E, LED1.cathode
  N9: Q1.B, R4.Pin_0
  N10: LED1.anode, R3.Pin_1
  N11: LED2.cathode, R5.Pin_0
